// Logisim project Processor_final.circ as structural Verilog: 5 circuits, main circuit main
module main (
);

  wire ALUcontrol, and_2_out, branch, branch_control, branch_true, call, clk, clock_1_out, ImmediateControl,
       jmp, li_control, live, MemRead, MemWrite, move, or_2_out, read, reboot, rtn, set, special_signal,
       store, write;
  wire [2:0] bit_extender_2_out, multiplexer_4_out, multiplexer_5_out;
  wire [4:0] immediate, opcode;
  wire [7:5] li;
  wire [10:8] x;
  wire [15:0] adder_1_out, adder_2_out, adder_3_out, ALUData, Aludata1, Aludata2, bit_extender_1_out,
       bit_extender_3_out, branch_jump, multiplexer_1_out, multiplexer_2_out, multiplexer_3_out,
       multiplexer_6_out, multiplexer_7_out, multiplexer_8_out, multiplexer_10_out, pcval, ra_q, ram_1_data,
       register_file_dataread2;

  // Probe on multiplexer_3_out
  Register #(.width(16), .trigger("falling")) pc (.D(multiplexer_3_out), .en(1'b1), .Q(pcval), .clk(clk), .clr(reboot));
  and and_1 (clk, clock_1_out, ~live);  // AND_Gate
  Adder #(.width(16)) adder_1 (.a(pcval), .b(16'h1), .out(adder_1_out));  // open: cin, cout
  and and_2 (and_2_out, clk, call);
  assign bit_extender_1_out = {{5{x[10]}}, {x, li, immediate}};  // Bit_Extender bit_extender_1
  // Probe on adder_1_out
  Multiplexer #(.width(16), .enable("false")) multiplexer_1 (
    .in0(bit_extender_1_out), .in1(branch_jump), .out(multiplexer_1_out), .sel(branch_control));
  Adder #(.width(16)) adder_2 (.a(pcval), .b(16'h1), .out(adder_2_out));  // open: cin, cout
  Adder #(.width(16)) adder_3 (.a(multiplexer_1_out), .b(pcval), .out(adder_3_out));  // open: cin, cout
  or or_1 (special_signal, branch_control, jmp, rtn, call);
  ROM #(.addrWidth(16), .dataWidth(16)) rom_1 (.addr(pcval), .data({opcode, x, li, immediate}));  // open: sel
  Clock clock_1 (.out(clock_1_out));
  Register #(.width(16)) ra (.D(adder_2_out), .en(call), .Q(ra_q), .clk(and_2_out));  // open: clr
  Multiplexer #(.width(16), .enable("false")) multiplexer_2 (
    .in0(adder_1_out), .in1(adder_3_out), .out(multiplexer_2_out), .sel(special_signal));
  // Probe on adder_1_out
  Multiplexer #(.width(16), .enable("false")) multiplexer_3 (
    .in0(multiplexer_2_out), .in1(ra_q), .out(multiplexer_3_out), .sel(rtn));
  // Probe on {x, li, immediate}
  // Probe on {opcode, x, li, immediate}
  // Probe on opcode
  // Probe on bit_extender_2_out
  // Probe on Aludata2
  // Probe on multiplexer_3_out
  or or_2 (or_2_out, branch, store);
  // Probe on li
  // Probe on Aludata1
  ALU ALU (.Data1(Aludata1), .Data2(Aludata2), .Mod_op(opcode[3:0]), .Aludata(ALUData), .branch_true(branch_true));
  // Probe on Aludata2
  // Probe on x
  Bit_Extender #(.in_width(5), .out_width(3)) bit_extender_2 (.in(immediate), .out(bit_extender_2_out));
  and and_3 (branch_control, branch, branch_true);
  Multiplexer #(.width(3), .enable("false")) multiplexer_4 (.in0(li), .in1(x), .out(multiplexer_4_out), .sel(or_2_out));
  Multiplexer #(.width(3), .enable("false")) multiplexer_5 (
    .in0(bit_extender_2_out), .in1(li), .out(multiplexer_5_out), .sel(branch));
  assign bit_extender_3_out = {{8{1'b0}}, {li, immediate}};  // Bit_Extender bit_extender_3
  control control (
    .in_1(opcode), .rr(read), .rw(write), .memr(MemRead), .memw(MemWrite), .alu(ALUcontrol), .jmp(jmp),
    .call(call), .reboot(reboot), .halt(live), .rtn(rtn), .immediate(ImmediateControl), .li(li_control));
  // Probe on ALUData
  Multiplexer #(.width(16), .enable("false")) multiplexer_6 (
    .in0(multiplexer_10_out), .in1(bit_extender_3_out), .out(multiplexer_6_out), .sel(li_control));
  // Probe on immediate
  control_two second_control (.opcode(opcode), .branch(branch), .set_on_less_than(set), .store(store), .move(move));
  Multiplexer #(.width(16), .enable("false")) multiplexer_7 (
    .in0(multiplexer_6_out), .in1(ALUData), .out(multiplexer_7_out), .sel(set));
  assign branch_jump = {{11{immediate[4]}}, immediate};  // Bit_Extender bit_extender_4
  RAM #(.addrWidth(16), .dataWidth(16), .bus("separate")) ram_1 (
    .addr(Aludata2), .din(Aludata1), .data(ram_1_data), .str(MemWrite), .clk(clk), .ld(MemRead));  // open: sel, clr
  registerfile register_file (
    .Write(write), .WriteRegister(x), .Read(read), .Readregister1(multiplexer_4_out),
    .Readregister2(multiplexer_5_out), .RegisterData(multiplexer_7_out), .Clock(clk), .reboot(reboot),
    .DataRead1(Aludata1), .DataRead2(register_file_dataread2));
  // Probe on multiplexer_7_out
  // Probe on Aludata1
  // Probe on branch_jump
  Multiplexer #(.width(16), .enable("false")) multiplexer_8 (
    .in0(ram_1_data), .in1(ALUData), .out(multiplexer_8_out), .sel(ALUcontrol));
  // Probe on ram_1_data
  Multiplexer #(.width(16), .enable("false")) multiplexer_9 (
    .in0(register_file_dataread2), .in1(branch_jump), .out(Aludata2), .sel(ImmediateControl));
  Multiplexer #(.width(16), .enable("false")) multiplexer_10 (
    .in0(multiplexer_8_out), .in1(Aludata1), .out(multiplexer_10_out), .sel(move));
  // Probe on multiplexer_10_out
  // Probe on Aludata2
  // Probe on multiplexer_10_out
  // Probe on ImmediateControl

  // Other names for the same wires on the sheet: li[4:0] = immediate; x[7:0] = {li, immediate};
  //   MemAddr[15:0] = Aludata2; MemData[15:0] = Aludata1; RegData1[15:0] = Aludata1

  // Notes on the sheet:
  //   contents of rom_1 (hex, n*v repeats v):
  //   6003 6105 4203 5348 1403 1d80 2681 9800
endmodule

module control (
  input  [4:0] in_1,
  output rr,
  output rw,
  output memr,
  output memw,
  output alu,
  output jmp,
  output call,
  output reboot,
  output halt,
  output rtn,
  output immediate,
  output li
);

  wire and_1_out, and_2_out, and_3_out, and_4_out, and_5_out, and_6_out, and_7_out, and_8_out, and_11_out,
       and_12_out, and_13_out, and_19_out, and_20_out, and_21_out, not_1_out, not_2_out, not_3_out,
       not_4_out, not_5_out, not_6_out, not_7_out, not_8_out, not_9_out, not_10_out, not_11_out, not_12_out,
       not_13_out, not_14_out, not_15_out, not_16_out, not_17_out, not_18_out, not_19_out, not_20_out,
       not_21_out, not_22_out, not_23_out, not_24_out, not_25_out, not_26_out, not_27_out, not_28_out,
       not_29_out, not_30_out, not_31_out, not_32_out, not_33_out, not_34_out, not_35_out, not_36_out,
       not_37_out, not_38_out, not_39_out, not_40_out, not_41_out, not_42_out, not_43_out, not_44_out,
       not_45_out, not_46_out, not_47_out, not_48_out, not_49_out, not_50_out, not_51_out, not_52_out,
       not_53_out, not_54_out, not_55_out;

  not not_1 (not_1_out, in_1[4]);
  not not_2 (not_2_out, in_1[3]);
  not not_3 (not_3_out, in_1[4]);
  not not_4 (not_4_out, in_1[2]);
  not not_5 (not_5_out, in_1[4]);
  not not_6 (not_6_out, in_1[1]);
  not not_7 (not_7_out, in_1[4]);
  not not_8 (not_8_out, in_1[0]);
  not not_9 (not_9_out, in_1[4]);
  not not_10 (not_10_out, in_1[3]);
  not not_11 (not_11_out, in_1[1]);
  not not_12 (not_12_out, in_1[4]);
  not not_13 (not_13_out, in_1[2]);
  not not_14 (not_14_out, in_1[4]);
  not not_15 (not_15_out, in_1[3]);
  not not_16 (not_16_out, in_1[4]);
  not not_17 (not_17_out, in_1[0]);
  not not_18 (not_18_out, in_1[4]);
  not not_19 (not_19_out, in_1[2]);
  not not_20 (not_20_out, in_1[4]);
  not not_21 (not_21_out, in_1[1]);
  not not_22 (not_22_out, in_1[4]);
  not not_23 (not_23_out, in_1[3]);
  not not_24 (not_24_out, in_1[4]);
  not not_25 (not_25_out, in_1[2]);
  not not_26 (not_26_out, in_1[1]);
  not not_27 (not_27_out, in_1[4]);
  not not_28 (not_28_out, in_1[2]);
  not not_29 (not_29_out, in_1[0]);
  not not_30 (not_30_out, in_1[4]);
  not not_31 (not_31_out, in_1[3]);
  not not_32 (not_32_out, in_1[2]);
  not not_33 (not_33_out, in_1[1]);
  not not_34 (not_34_out, in_1[0]);
  not not_35 (not_35_out, in_1[3]);
  not not_36 (not_36_out, in_1[2]);
  not not_37 (not_37_out, in_1[0]);
  not not_38 (not_38_out, in_1[3]);
  not not_39 (not_39_out, in_1[2]);
  not not_40 (not_40_out, in_1[3]);
  not not_41 (not_41_out, in_1[2]);
  not not_42 (not_42_out, in_1[1]);
  not not_43 (not_43_out, in_1[4]);
  not not_44 (not_44_out, in_1[3]);
  not not_45 (not_45_out, in_1[2]);
  not not_46 (not_46_out, in_1[1]);
  not not_47 (not_47_out, in_1[4]);
  not not_48 (not_48_out, in_1[2]);
  not not_49 (not_49_out, in_1[0]);
  not not_50 (not_50_out, in_1[4]);
  not not_51 (not_51_out, in_1[1]);
  not not_52 (not_52_out, in_1[0]);
  not not_53 (not_53_out, in_1[4]);
  not not_54 (not_54_out, in_1[1]);
  not not_55 (not_55_out, in_1[0]);
  and and_1 (and_1_out, not_1_out, not_2_out);
  and and_2 (and_2_out, not_3_out, not_4_out);
  and and_3 (and_3_out, not_5_out, not_6_out, in_1[0]);
  and and_4 (and_4_out, not_7_out, in_1[1], not_8_out);
  and and_5 (and_5_out, not_9_out, not_10_out, not_11_out);
  and and_6 (and_6_out, not_12_out, not_13_out);
  and and_7 (and_7_out, not_14_out, not_15_out, in_1[0]);
  and and_8 (and_8_out, not_16_out, in_1[3], not_17_out);
  and and_9 (memr, not_18_out, in_1[3], not_19_out, in_1[1], in_1[0]);
  and and_10 (memw, not_20_out, in_1[3], in_1[2], not_21_out, in_1[0]);
  and and_11 (and_11_out, not_22_out, not_23_out);
  and and_12 (and_12_out, not_24_out, not_25_out, not_26_out);
  and and_13 (and_13_out, not_27_out, not_28_out, not_29_out);
  and and_14 (jmp, not_30_out, in_1[3], in_1[2], in_1[1], in_1[0]);
  and and_15 (call, in_1[4], not_31_out, not_32_out, not_33_out, not_34_out);
  and and_16 (reboot, in_1[4], not_35_out, not_36_out, in_1[1], not_37_out);
  and and_17 (halt, in_1[4], not_38_out, not_39_out, in_1[1], in_1[0]);
  and and_18 (rtn, in_1[4], not_40_out, not_41_out, not_42_out, in_1[0]);
  and and_19 (and_19_out, not_43_out, not_44_out, not_45_out, not_46_out, in_1[0]);
  and and_20 (and_20_out, not_47_out, in_1[3], not_48_out, not_49_out);
  and and_21 (and_21_out, not_50_out, in_1[3], not_51_out, not_52_out);
  and and_22 (li, not_53_out, in_1[3], in_1[2], not_54_out, not_55_out);
  or or_1 (rr, and_1_out, and_2_out, and_3_out, and_4_out);
  or or_2 (rw, and_5_out, and_6_out, and_7_out, and_8_out);
  or or_3 (alu, and_11_out, and_12_out, and_13_out);
  or or_4 (immediate, and_19_out, and_20_out, and_21_out);
endmodule

module registerfile (
  input  Write,
  input  [2:0] WriteRegister,
  input  Read,
  input  [2:0] Readregister1,
  input  [2:0] Readregister2,
  input  [15:0] RegisterData,
  input  Clock,
  input  reboot,
  output [15:0] DataRead1,
  output [15:0] DataRead2
);

  wire and_1_out, and_2_out, and_3_out, and_4_out, and_5_out, and_6_out, and_7_out, and_8_out,
       decoder_1_out0, decoder_1_out1, decoder_1_out2, decoder_1_out3, decoder_1_out4, decoder_1_out5,
       decoder_1_out6, decoder_1_out7;
  wire [15:0] r1_q, r2_q, r3_q, r4_q, r5_q, r6_q, r7_q, r8_q;

  Decoder #(.select(3)) decoder_1 (
    .out0(decoder_1_out0), .out1(decoder_1_out1), .out2(decoder_1_out2), .out3(decoder_1_out3),
    .out4(decoder_1_out4), .out5(decoder_1_out5), .out6(decoder_1_out6), .out7(decoder_1_out7),
    .sel(WriteRegister), .en(1'b1));
  // Probe on RegisterData
  and and_1 (and_1_out, decoder_1_out0, Write);
  and and_2 (and_2_out, decoder_1_out1, Write);
  and and_3 (and_3_out, decoder_1_out2, decoder_1_out2, Write);
  and and_4 (and_4_out, decoder_1_out3, Write);
  and and_5 (and_5_out, decoder_1_out4, Write);
  and and_6 (and_6_out, decoder_1_out5, Write);
  and and_7 (and_7_out, decoder_1_out6, Write);
  and and_8 (and_8_out, decoder_1_out7, Write);
  Register #(.width(16)) r1 (.D(RegisterData), .en(and_1_out), .Q(r1_q), .clk(Clock), .clr(reboot));
  Register #(.width(16)) r2 (.D(RegisterData), .en(and_2_out), .Q(r2_q), .clk(Clock), .clr(reboot));
  Register #(.width(16)) r3 (.D(RegisterData), .en(and_3_out), .Q(r3_q), .clk(Clock), .clr(reboot));
  Register #(.width(16)) r4 (.D(RegisterData), .en(and_4_out), .Q(r4_q), .clk(Clock), .clr(reboot));
  Register #(.width(16)) r5 (.D(RegisterData), .en(and_5_out), .Q(r5_q), .clk(Clock), .clr(reboot));
  Register #(.width(16)) r6 (.D(RegisterData), .en(and_6_out), .Q(r6_q), .clk(Clock), .clr(reboot));
  Register #(.width(16)) r7 (.D(RegisterData), .en(and_7_out), .Q(r7_q), .clk(Clock), .clr(reboot));
  Register #(.width(16)) r8 (.D(RegisterData), .en(and_8_out), .Q(r8_q), .clk(Clock), .clr(reboot));
  // Probe on r1_q
  Multiplexer #(.select(3), .width(16)) multiplexer_1 (
    .in0(r1_q), .in1(r2_q), .in2(r3_q), .in3(r4_q), .in4(r5_q), .in5(r6_q), .in6(r7_q), .in7(r8_q),
    .out(DataRead1), .sel(Readregister1), .en(Read));
  Multiplexer #(.select(3), .width(16)) multiplexer_2 (
    .in0(r1_q), .in1(r2_q), .in2(r3_q), .in3(r4_q), .in4(r5_q), .in5(r6_q), .in6(r7_q), .in7(r8_q),
    .out(DataRead2), .sel(Readregister2), .en(Read));
  // Probe on r8_q
endmodule

module ALU (
  input  [15:0] Data1,
  input  [15:0] Data2,
  input  [3:0] Mod_op,
  output [15:0] Aludata,
  output branch_true
);

  wire comparator_1_lt, comparator_2_eq, comparator_3_gt;
  wire [15:0] adder_1_out, and_1_out, bit_extender_1_out, bit_extender_2_out, lsl, lsr, negator_1_out,
       or_1_out, result_1, result_2, subtractor_1_out;

  Adder #(.width(16)) adder_1 (.a(Data1), .b(Data2), .out(adder_1_out));  // open: cin, cout
  Subtractor #(.width(16)) subtractor_1 (.a(Data1), .b(Data2), .out(subtractor_1_out));  // open: bin, bout
  Negator #(.width(16)) negator_1 (.in(Data1), .out(negator_1_out));
  Shifter #(.width(16)) shifter_1 (.in(Data1), .\dist (Data2[3:0]), .out(lsl));
  Shifter #(.width(16), .shift("lr")) shifter_2 (.in(Data1), .\dist (Data2[3:0]), .out(lsr));
  Comparator #(.width(16)) comparator_1 (.a(Data1), .b(Data2), .lt(comparator_1_lt));  // open: gt, eq
  Comparator #(.width(16)) comparator_2 (.a(Data1), .b(Data2), .eq(comparator_2_eq));  // open: gt, lt
  assign bit_extender_1_out = {{15{1'b0}}, comparator_1_lt};  // Bit_Extender bit_extender_1
  assign and_1_out = Data1 & Data2;  // AND_Gate and_1, 16 bits wide
  assign or_1_out = Data1 | Data2;  // OR_Gate or_1, 16 bits wide
  or or_2 (branch_true, comparator_1_lt, comparator_2_eq);
  Comparator #(.width(16)) comparator_3 (.a(Data2), .b(16'hf), .gt(comparator_3_gt));  // open: eq, lt
  assign bit_extender_2_out = {{15{1'b0}}, branch_true};  // Bit_Extender bit_extender_2
  Multiplexer #(.width(16), .enable("false")) multiplexer_1 (
    .in0(lsl), .in1({16{1'b0}}), .out(result_1), .sel(comparator_3_gt));
  Multiplexer #(.width(16), .enable("false")) multiplexer_2 (
    .in0(lsr), .in1({16{1'b0}}), .out(result_2), .sel(comparator_3_gt));
  Multiplexer #(.select(4), .width(16), .enable("false")) multiplexer_3 (
    .in0(adder_1_out), .in1(adder_1_out), .in2(negator_1_out), .in3(result_1), .in4(result_2),
    .in5(bit_extender_1_out), .in6(bit_extender_2_out), .in7(and_1_out), .in8(and_1_out), .in9(or_1_out),
    .in10(or_1_out), .in11({16{1'b0}}), .in12({16{1'b0}}), .in13({16{1'b0}}), .in14({16{1'b0}}),
    .in15({16{1'b0}}), .out(Aludata), .sel(Mod_op));
endmodule

module control_two (
  input  [4:0] opcode,
  output branch,
  output set_on_less_than,
  output store,
  output move
);

  wire nand_1_out, nand_2_out, nand_3_out, nand_4_out, nand_5_out, nand_6_out, nand_7_out, nand_8_out,
       nand_9_out, nand_10_out, nand_11_out, nand_12_out, nand_13_out, nand_14_out, nand_15_out, nand_16_out,
       nand_17_out, nand_18_out, nand_19_out, nand_20_out, nand_21_out, nand_22_out, nand_23_out,
       nand_24_out, nand_25_out;

  nand nand_1 (nand_1_out, opcode[4], opcode[4]);
  nand nand_2 (nand_2_out, opcode[3], opcode[3]);
  nand nand_3 (nand_3_out, opcode[0], opcode[0]);
  nand nand_4 (nand_4_out, opcode[4], opcode[4]);
  nand nand_5 (nand_5_out, opcode[3], opcode[3]);
  nand nand_6 (nand_6_out, opcode[0], opcode[0]);
  nand nand_7 (nand_7_out, opcode[4], opcode[4]);
  nand nand_8 (nand_8_out, opcode[3], opcode[3]);
  nand nand_9 (nand_9_out, opcode[1], opcode[1]);
  nand nand_10 (nand_10_out, opcode[4], opcode[4]);
  nand nand_11 (nand_11_out, opcode[3], opcode[3]);
  nand nand_12 (nand_12_out, opcode[1], opcode[1]);
  nand nand_13 (nand_13_out, opcode[4], opcode[4]);
  nand nand_14 (nand_14_out, opcode[1], opcode[1]);
  nand nand_15 (nand_15_out, opcode[4], opcode[4]);
  nand nand_16 (nand_16_out, opcode[1], opcode[1]);
  nand nand_17 (nand_17_out, opcode[4], opcode[4]);
  nand nand_18 (nand_18_out, opcode[0], opcode[0]);
  nand nand_19 (nand_19_out, nand_1_out, nand_2_out, opcode[2], opcode[1], nand_3_out);
  nand nand_20 (nand_20_out, nand_4_out, nand_5_out, opcode[2], opcode[1], nand_6_out);
  nand nand_21 (nand_21_out, nand_7_out, nand_8_out, opcode[2], nand_9_out, opcode[0]);
  nand nand_22 (nand_22_out, nand_10_out, nand_11_out, opcode[2], nand_12_out, opcode[0]);
  nand nand_23 (nand_23_out, nand_13_out, opcode[3], opcode[2], nand_14_out, opcode[0]);
  nand nand_24 (nand_24_out, nand_15_out, opcode[3], opcode[2], nand_16_out, opcode[0]);
  nand nand_25 (nand_25_out, nand_17_out, opcode[3], opcode[2], opcode[1], nand_18_out);
  nand nand_26 (branch, nand_19_out, nand_20_out);
  nand nand_27 (set_on_less_than, nand_21_out, nand_22_out);
  nand nand_28 (store, nand_23_out, nand_24_out);
  nand nand_29 (move, nand_25_out, nand_25_out);
endmodule
